// Logisim project computer_made_with_logisim.circ as structural Verilog
// cAnd
module \and  (
  input  in_1,
  input  in_2,
  output out_3
);

  wire nand_1_out;

  nand nand_1 (nand_1_out, in_1, in_2);
  \not  not_1 (.in_1(nand_1_out), .out_2(out_3));
endmodule

// cNot
module \not  (
  input  in_1,
  output out_2
);

  nand nand_1 (out_2, in_1, in_1);
endmodule

// cOr
module \or  (
  input  in_1,
  input  in_2,
  output out_3
);

  wire not_1_out_2, not_2_out_2;

  \not  not_1 (.in_1(in_1), .out_2(not_1_out_2));
  \not  not_2 (.in_1(in_2), .out_2(not_2_out_2));
  nand nand_1 (out_3, not_1_out_2, not_2_out_2);
endmodule

// cXor
module \xor  (
  input  in_1,
  input  in_2,
  output out_3
);

  wire and_1_out_3, and_2_out_3, not_1_out_2, not_2_out_2;

  \and  and_1 (.in_1(in_1), .in_2(not_1_out_2), .out_3(and_1_out_3));
  \not  not_1 (.in_1(in_2), .out_2(not_1_out_2));
  \not  not_2 (.in_1(in_1), .out_2(not_2_out_2));
  \and  and_2 (.in_1(not_2_out_2), .in_2(in_2), .out_3(and_2_out_3));
  \or  or_1 (.in_1(and_1_out_3), .in_2(and_2_out_3), .out_3(out_3));
endmodule

// cOr8Way
module or8way (
  input  [7:0] in_1,
  output out_2
);

  wire or_1_out, or_2_out, or_3_out, or_4_out, or_5_out, or_6_out;

  or or_1 (or_1_out, in_1[0], in_1[1]);
  or or_2 (or_2_out, or_1_out, in_1[2]);
  or or_3 (or_3_out, or_2_out, in_1[3]);
  or or_4 (or_4_out, or_3_out, in_1[4]);
  or or_5 (or_5_out, or_4_out, in_1[5]);
  or or_6 (or_6_out, or_5_out, in_1[6]);
  or or_7 (out_2, or_6_out, in_1[7]);
endmodule

// cAnd16
module and16 (
  input  [15:0] in_1,
  input  [15:0] in_2,
  output [15:0] out_3
);

  and and_1 (out_3[0], in_1[0], in_2[0]);
  and and_2 (out_3[1], in_1[1], in_2[1]);
  and and_3 (out_3[2], in_1[2], in_2[2]);
  and and_4 (out_3[3], in_1[3], in_2[3]);
  and and_5 (out_3[4], in_1[4], in_2[4]);
  and and_6 (out_3[5], in_1[5], in_2[5]);
  and and_7 (out_3[6], in_1[6], in_2[6]);
  and and_8 (out_3[7], in_1[7], in_2[7]);
  and and_9 (out_3[8], in_1[8], in_2[8]);
  and and_10 (out_3[9], in_1[9], in_2[9]);
  and and_11 (out_3[10], in_1[10], in_2[10]);
  and and_12 (out_3[11], in_1[11], in_2[11]);
  and and_13 (out_3[12], in_1[12], in_2[12]);
  and and_14 (out_3[13], in_1[13], in_2[13]);
  and and_15 (out_3[14], in_1[14], in_2[14]);
  and and_16 (out_3[15], in_1[15], in_2[15]);
endmodule

module mux (
  input  a,
  input  b,
  input  sel,
  output out
);

  wire and_1_out, and_2_out, not_1_out;

  not not_1 (not_1_out, sel);
  and and_1 (and_1_out, a, not_1_out);
  and and_2 (and_2_out, b, sel);
  or or_1 (out, and_1_out, and_2_out);

  // Notes on the sheet:
  //   if sel == 0 then out = a else out = b
endmodule

module mux4way (
  input  a,
  input  b,
  input  c,
  input  d,
  input  [1:0] sel,
  output out_6
);

  wire and_1_out, and_2_out, and_3_out, and_4_out, and_5_out, and_6_out, and_7_out, and_8_out, not_1_out,
       not_2_out, not_3_out, not_4_out, or_1_out, or_2_out;

  not not_1 (not_1_out, sel[0]);
  and and_1 (and_1_out, not_1_out, not_2_out);
  not not_2 (not_2_out, sel[1]);
  and and_2 (and_2_out, sel[0], not_3_out);
  not not_3 (not_3_out, sel[1]);
  not not_4 (not_4_out, sel[0]);
  and and_3 (and_3_out, not_4_out, sel[1]);
  and and_4 (and_4_out, sel[0], sel[1]);
  and and_5 (and_5_out, and_1_out, a);
  and and_6 (and_6_out, and_2_out, b);
  and and_7 (and_7_out, and_3_out, c);
  and and_8 (and_8_out, and_4_out, d);
  or or_1 (or_1_out, and_5_out, and_6_out);
  or or_2 (or_2_out, and_7_out, and_8_out);
  or or_3 (out_6, or_1_out, or_2_out);

  // Notes on the sheet:
  //   out = a if sel == 00 
  //   = b if sel == 01
  //   = c if sel == 10
  //   = d if sel == 11
endmodule

module dmux (
  input  in_1,
  input  sel,
  output out_3,
  output out_4
);

  wire not_1_out;

  and and_1 (out_3, in_1, not_1_out);
  not not_1 (not_1_out, sel);
  and and_2 (out_4, in_1, sel);
endmodule

module dmux4way (
  input  in_1,
  input  [1:0] sel,
  output out_3,
  output out_4,
  output out_5,
  output out_6
);

  wire and_1_out, and_2_out, and_3_out, and_4_out, not_1_out, not_2_out, not_3_out, not_4_out;

  not not_1 (not_1_out, sel[0]);
  not not_2 (not_2_out, sel[1]);
  not not_3 (not_3_out, sel[1]);
  not not_4 (not_4_out, sel[0]);
  and and_1 (and_1_out, not_1_out, not_2_out);
  and and_2 (and_2_out, sel[0], not_3_out);
  and and_3 (and_3_out, not_4_out, sel[1]);
  and and_4 (and_4_out, sel[0], sel[1]);
  and and_5 (out_3, and_1_out, in_1);
  and and_6 (out_4, and_2_out, in_1);
  and and_7 (out_5, and_3_out, in_1);
  and and_8 (out_6, and_4_out, in_1);
endmodule

module halfadder (
  input  a,
  input  b,
  output sum,
  output carry
);

  xor xor_1 (sum, a, b);
  and and_1 (carry, a, b);
endmodule

module fulladder (
  input  carry,
  input  a,
  input  b,
  output sum,
  output ca
);

  wire halfadder_1_carry, halfadder_1_sum, halfadder_2_carry;

  halfadder halfadder_1 (.a(a), .b(b), .sum(halfadder_1_sum), .carry(halfadder_1_carry));
  halfadder halfadder_2 (.a(carry), .b(halfadder_1_sum), .sum(sum), .carry(halfadder_2_carry));
  or or_1 (ca, halfadder_2_carry, halfadder_1_carry);
endmodule

module adder4 (
  input  in_1,
  input  [3:0] a,
  input  [3:0] b,
  output [3:0] sum,
  output carry
);

  wire fulladder_1_ca, fulladder_2_ca, fulladder_3_ca;

  fulladder fulladder_1 (.carry(in_1), .a(a[0]), .b(b[0]), .sum(sum[0]), .ca(fulladder_1_ca));
  fulladder fulladder_2 (.carry(fulladder_1_ca), .a(a[1]), .b(b[1]), .sum(sum[1]), .ca(fulladder_2_ca));
  fulladder fulladder_3 (.carry(fulladder_2_ca), .a(a[2]), .b(b[2]), .sum(sum[2]), .ca(fulladder_3_ca));
  fulladder fulladder_4 (.carry(fulladder_3_ca), .a(a[3]), .b(b[3]), .sum(sum[3]), .ca(carry));
endmodule

module adder8 (
  input  cin,
  input  [7:0] a,
  input  [7:0] b,
  output [7:0] sum,
  output cout
);

  wire adder4_1_carry;

  adder4 adder4_1 (.in_1(cin), .a(a[3:0]), .b(b[3:0]), .sum(sum[3:0]), .carry(adder4_1_carry));
  adder4 adder4_2 (.in_1(adder4_1_carry), .a(a[7:4]), .b(b[7:4]), .sum(sum[7:4]), .carry(cout));
endmodule

module adder16 (
  input  [15:0] a,
  input  [15:0] b,
  output [15:0] sum,
  output cout
);

  wire adder8_1_cout;

  adder8 adder8_1 (.cin(1'b0), .a(a[7:0]), .b(b[7:0]), .sum(sum[7:0]), .cout(adder8_1_cout));
  adder8 adder8_2 (.cin(adder8_1_cout), .a(a[15:8]), .b(b[15:8]), .sum(sum[15:8]), .cout(cout));
endmodule
